# Fritzing sketch sketch (saved by Fritzing 0.4.3b)
breadboards: 1

parts:
  Arduino1 = Arduino
  S1 = Pushbutton [package="[THT]"]
  R1 = 10k Ω Resistor [package=THT]

nets:
  N1: Arduino1.GND, R1.Pin_1
  N2: Arduino1.D2, S1.Pin_1, S1.Pin_2, R1.Pin_0
  N3: Arduino1.+5V, S1.Pin_3, S1.Pin_4
